# Fritzing sketch iot (saved by Fritzing 0.9.3b)
breadboards: 1

parts:
  Part1 = Arduino Uno (Rev3)
  LED1 = 7-SEGMENT-4DIGIT-YOUNGSUN [package=7-segment-4digit-youngsun-longpads]
  U1 = MAX7219 [package=dil24]
  R1 = Resistor [tolerance=±5% resistance=1k package=THT]
  RF_TX = RF-LINK_TX [package=rf-link_tx]
  Touch_Sensor = IR Receiver Breakout [package=PCB]
  DHT11 = TMP36 [package=to-92]
  Ethernet_shield = Arduino Ethernet Shield (Rev3)  # not connected
  RTC = Real Time Clock Module - DS1307 RTC Breakout Board
  LDR = Photocell (LDR) [package=THT]
  R2 = Resistor [tolerance=±5% resistance=10k package=THT]

nets:
  N1: Part1.A0, LDR.pin_1, R2.Pin_1
  N2: Part1.A4/SDA, RTC.SDA
  N3: Part1.A5/SCL, RTC.SCL
  N4: Part1.D2, U1.CLK
  N5: Part1.D3_PWM, U1.DIN
  N6: Part1.D4, U1.LOAD
  N7: Part1.D5_PWM, RF_TX.DATA
  N8: Part1.D6_PWM, Touch_Sensor.VCC
  N9: Part1.D7, DHT11.VCC
  5V: Part1.5V, U1.VCC, R1.Pin_0, RF_TX.+5V, Touch_Sensor.OUT, DHT11.VOUT, RTC.5V, LDR.pin_0
  GND: Part1.GND, U1.GND, U1.GND2, RF_TX.ANT, Touch_Sensor.GND, DHT11.GND, RTC.GND, R2.Pin_0
  N10: LED1.DIG1, U1.SEGE
  N11: LED1.DIG2, U1.SEGD
  N12: LED1.D, U1.SEGDP
  N13: LED1.DIG3, U1.SEGC
  N14: LED1.DP, U1.SEGG
  N15: LED1.DIG4, U1.DIG3
  N16: LED1.APOS-C, U1.SEGB
  N17: LED1.APOS-A, U1.DIG2
  N18: LED1.F, U1.DIG1
  N19: LED1.A, U1.SEGF
  N20: LED1.G, U1.SEGA
  N21: LED1.B, U1.DIG0
  N22: U1.ISET, R1.Pin_1
