# Fritzing sketch iotv2 (saved by Fritzing 0.9.3b)
breadboards: 1

parts:
  Part1 = Arduino Uno (Rev3)
  LED1 = 7-SEGMENT-4DIGIT-YOUNGSUN [package=7-segment-4digit-youngsun-longpads]
  R1 = Resistor [tolerance=±5% resistance=1k package=THT]
  RF_TX = RF-LINK_TX [package=rf-link_tx]
  DHT11 = TMP36 [package=to-92]
  Ethernet_shield = Arduino Ethernet Shield (Rev3)  # not connected
  RTC = Real Time Clock Module - DS1307 RTC Breakout Board
  LDR = Photocell (LDR) [package=THT]
  R2 = Resistor [tolerance=±5% resistance=10k package=THT]
  U2 = 74HC595 [package="DIP16 [THT]"]
  hc-sr1 = hc-sr04
  U3 = 74HC595 [package="DIP16 [THT]"]  # not connected
  J1 = Piezo Speaker

nets:
  N1: Part1.A0, DHT11.VCC
  N2: Part1.A1, LDR.pin_1, R2.Pin_1
  N3: Part1.A4/SDA, RTC.SDA
  N4: Part1.A5/SCL, RTC.SCL
  N5: Part1.D2, RF_TX.DATA
  5V: Part1.5V, R1.Pin_0, RF_TX.+5V, DHT11.VOUT, RTC.5V, LDR.pin_0, hc-sr1.VCC
  GND: Part1.GND, RF_TX.ANT, DHT11.GND, RTC.GND, R2.Pin_0, hc-sr1.GND, J1.pin1
  N6: LED1.DIG3, U2.VCC
  N7: LED1.DP, U2.OE
  N8: LED1.APOS-C, U2.ST_CP
  N9: LED1.A, U2.SH_CP
  N10: LED1.G, U2.MR
  N11: R1.Pin_1, U2.DS
